# Fritzing sketch eksamen (saved by Fritzing 0.9.3b)
breadboards: 1

parts:
  Part1 = Photon
  J1 = male pin header, 3 pins [form="♂ (male)"]
  DHT1 = DHT11 Humitidy and Temperature Sensor
  R1 = Resistor [tolerance=±5% resistance=10k package=THT]
  LED1 = LED - 5mm [color="Green (560nm)" package="5 mm [THT]"]
  LED2 = LED - 5mm [color="Yellow (592nm)" package="5 mm [THT]"]
  LED3 = LED - 5mm [color="Red (633nm)" package="5 mm [THT]"]
  R2 = Resistor [tolerance=±5% resistance=330 package=THT]
  R3 = Resistor [tolerance=±5% resistance=330 package=THT]
  R4 = Resistor [tolerance=±5% resistance=330 package=THT]

nets:
  N1: Part1.A0, J1.pin1
  GND: Part1.GND, J1.pin3, DHT1.GND, R2.Pin_0, R3.Pin_0, R4.Pin_0
  VIN: Part1.VIN, J1.pin2, DHT1.VDD, R1.Pin_0
  N2: Part1.D0, LED3.anode
  N3: Part1.D1, LED2.anode
  N4: Part1.D2, LED1.anode
  N5: Part1.D5, DHT1.DATA, R1.Pin_1
  N6: LED1.cathode, R2.Pin_1
  N7: LED2.cathode, R3.Pin_1
  N8: LED3.cathode, R4.Pin_1

notes:
  Funduino Water Sensor

custom parts:
  DHT11 Humitidy and Temperature Sensor: DHT11 Humidity and Temperature Sensor
